# Fritzing sketch lab3 (saved by Fritzing 0.9.3b)
breadboards: 1

parts:
  41MUX_for_routing = IC, DIP package, 16 pins [chip_label=153]
  21MUX = IC, DIP package, 16 pins [chip_label=157]
  NAND = IC, DIP package, 14 pins [chip_label=00]
  NOR = IC, DIP package, 14 pins [chip_label=02]
  XOR = IC, DIP package, 14 pins [chip_label=86]
  NOT = IC, DIP package, 14 pins [chip_label=04]
  SR-B = IC, DIP package, 16 pins [chip_label="194 SR"]
  SR-A = IC, DIP package, 16 pins [chip_label="194 SR"]
  41MUX_for_computation = IC, DIP package, 16 pins [chip_label=153]
  NAND1 = IC, DIP package, 14 pins [chip_label=00]
  3_input_nand = IC, DIP package, 14 pins [chip_label=10]
  Flip_Flop_for_C0_and_C1 = IC, DIP package, 14 pins [chip_label=74]
  Flip_Flop_for_Q = IC, DIP package, 14 pins [chip_label=74]
  NAND2 = IC, DIP package, 14 pins [chip_label=00]

nets:
  GND: 41MUX_for_routing.pin1, 41MUX_for_routing.pin15, 21MUX.pin15, 41MUX_for_computation.pin13, 41MUX_for_computation.pin15
  R1: 41MUX_for_routing.pin2
  SR-B: 41MUX_for_routing.pin3, 41MUX_for_routing.pin10, 41MUX_for_routing.pin12, NAND.pin5, NOR.pin5, XOR.pin5, SR-B.pin12
  F(A, B): 41MUX_for_routing.pin4, 41MUX_for_routing.pin11, 21MUX.pin14, NOT.pin8
  SR-A: 41MUX_for_routing.pin5, 41MUX_for_routing.pin6, 41MUX_for_routing.pin13, NAND.pin4, NOR.pin4, XOR.pin4, SR-A.pin12
  A*: 41MUX_for_routing.pin7, SR-A.pin2
  B*: 41MUX_for_routing.pin9, SR-B.pin2
  R0: 41MUX_for_routing.pin14
  F2: 21MUX.pin1
  F'(A, B): 21MUX.pin13, NOT.pin9, 41MUX_for_computation.pin9
  A NAND B: NAND.pin6, 41MUX_for_computation.pin10
  A NOR B: NOR.pin6, 41MUX_for_computation.pin11
  A XOR B: NOR.pin8, NOR.pin9, XOR.pin6
  A XNOR B: NOR.pin10, 41MUX_for_computation.pin12
  C1+: XOR.pin8, Flip_Flop_for_C0_and_C1.pin12
  C1: XOR.pin9, NAND1.pin1, Flip_Flop_for_C0_and_C1.pin9
  C0: XOR.pin10, Flip_Flop_for_C0_and_C1.pin5
  Load A: NOT.pin1, SR-A.pin10
  (Load A)': NOT.pin2, NAND2.pin1
  Load B: NOT.pin3, SR-B.pin10
  (Load B)': NOT.pin4, NAND2.pin4
  Shift: NOT.pin5, 3_input_nand.pin6
  S': NOT.pin6, NAND2.pin2, NAND2.pin5
  5V: SR-B.pin1, SR-A.pin1, Flip_Flop_for_C0_and_C1.pin1, Flip_Flop_for_C0_and_C1.pin4, Flip_Flop_for_C0_and_C1.pin10, Flip_Flop_for_C0_and_C1.pin13, Flip_Flop_for_Q.pin1, Flip_Flop_for_Q.pin4
  D3: SR-B.pin3, SR-A.pin3
  D2: SR-B.pin4, SR-A.pin4
  D1: SR-B.pin5, SR-A.pin5
  D0: SR-B.pin6, SR-A.pin6
  S0-B: SR-B.pin9, NAND2.pin6
  CLK: SR-B.pin11, SR-A.pin11, Flip_Flop_for_C0_and_C1.pin3, Flip_Flop_for_C0_and_C1.pin11, Flip_Flop_for_Q.pin3
  S0-A: SR-A.pin9, NAND2.pin3
  F1: 41MUX_for_computation.pin2
  F0: 41MUX_for_computation.pin14
  C0': NAND1.pin2, 3_input_nand.pin1, 3_input_nand.pin5
  (C1C0')': NAND1.pin3, NAND1.pin13
  Execute: NAND1.pin4, 3_input_nand.pin9, 3_input_nand.pin10, 3_input_nand.pin11
  Q': NAND1.pin5, NAND1.pin9
  (EQ')': NAND1.pin6, NAND1.pin8, NAND1.pin12, 3_input_nand.pin3
  E': NAND1.pin10, 3_input_nand.pin8, 3_input_nand.pin13
  C0+: NAND1.pin11, Flip_Flop_for_C0_and_C1.pin2
  C1': 3_input_nand.pin2, 3_input_nand.pin4
  Q+: 3_input_nand.pin12, Flip_Flop_for_Q.pin2
